# Fritzing sketch sketch_capsense (saved by Fritzing 0.9.2b)
breadboards: 1

parts:
  パーツ1 = Arduino Uno (Rev3)
  R1 = Resistor [tolerance=±5% resistance=220 package=THT]
  LED1 = LED - 5mm [color="Red (633nm)" package="5 mm [THT]"]
  R2 = Resistor [tolerance=±5% resistance=1M package=THT]

nets:
  N1: パーツ1.GND, LED1.cathode
  N2: パーツ1.D2, R2.Pin_1
  N3: パーツ1.D4, R2.Pin_0
  N4: パーツ1.D6_PWM, R1.Pin_1
  N5: R1.Pin_0, LED1.anode

notes:
  銀紙/Papers
