# Fritzing sketch sketch_cds (saved by Fritzing 0.9.2b)
breadboards: 1

parts:
  パーツ1 = Arduino Uno (Rev3)
  R1 = Resistor [tolerance=±5% resistance=10k package=THT]
  J1 = Piezo Speaker
  R2 = PHOTOCELL [package=photocell]

nets:
  N1: パーツ1.A0, R1.Pin_0, R2.P$2
  N2: パーツ1.D12/MISO, J1.pin2
  N3: パーツ1.GND, J1.pin1, R2.P$1
  N4: パーツ1.5V, R1.Pin_1
