# Fritzing sketch sketch_depth (saved by Fritzing 0.9.2b)
breadboards: 1

parts:
  パーツ1 = Arduino Uno (Rev3)
  R1 = Resistor [tolerance=±5% resistance=220 package=THT]
  LED1 = LED - 5mm [color="Red (633nm)" package="5 mm [THT]"]
  J1 = Infrared Proximity Sensor
  C1 = Ceramic Capacitor [capacitance=100nF package="100 mil [THT, multilayer]"]

nets:
  N1: パーツ1.A0, J1.Vout, C1.0
  GND: パーツ1.GND, LED1.cathode, J1.GND, C1.1
  N2: パーツ1.D6_PWM, R1.Pin_1
  5V: パーツ1.5V, J1.Vcc
  N3: R1.Pin_0, LED1.anode
