# Fritzing sketch sketch_esp8266 (saved by Fritzing 0.9.2b)
breadboards: 1

parts:
  パーツ1 = Arduino Uno (Rev3)
  U1 = ESP8266 WiFi Module [part_number=ESP8266]

nets:
  N1: パーツ1.D2, U1.TXD
  N2: パーツ1.D3_PWM, U1.RXD
  3V3: パーツ1.3V3, U1.VCC, U1.CH_PD
  GND: パーツ1.GND, U1.GND

custom parts:
  ESP8266 WiFi Module: Generic WiFi Module based on the ESP8266 with onboard PCB antenna and UART communications
