# Fritzing sketch sketch_heartbeat (saved by Fritzing 0.9.2b)
breadboards: 1

parts:
  パーツ1 = Arduino Uno (Rev3) - ICSP
  LBR-127HLD = IC, DIP package, 4 pins [chip_label=LBR-127HLD]
  IC2 = IC, DIP package, 8 pins [chip_label=LM358N]
  R1 = Resistor [tolerance=±5% resistance=220 package=THT]
  R2 = Resistor [tolerance=±5% resistance=22k package=THT]
  C1 = Ceramic Capacitor [capacitance=10µF package="100 mil [THT, multilayer]"]
  R3 = Resistor [tolerance=±5% resistance=1k package=THT]
  R4 = Resistor [tolerance=±5% resistance=1k package=THT]
  C2 = Ceramic Capacitor [capacitance=1µF package="100 mil [THT, multilayer]"]
  R5 = Resistor [tolerance=±5% resistance=1k package=THT]
  C3 = Ceramic Capacitor [capacitance=0.1µF package="100 mil [THT, multilayer]"]

nets:
  N1: パーツ1.A0, IC2.pin1, C2.0, R5.Pin_0
  N2: パーツ1.5V, IC2.pin8, R1.Pin_1, R2.Pin_0, C3.1
  N3: パーツ1.GND, LBR-127HLD.pin2, LBR-127HLD.pin4, IC2.pin4, R3.Pin_1, R4.Pin_1, C3.0
  N4: LBR-127HLD.pin1, R1.Pin_0
  N5: LBR-127HLD.pin3, R2.Pin_1, C1.0
  N6: IC2.pin2, R4.Pin_0, C2.1, R5.Pin_1
  N7: IC2.pin3, C1.1, R3.Pin_0

notes:
  1
  2
  3
  4
