# Fritzing sketch sketch_led (saved by Fritzing 0.9.2b)
breadboards: 1

parts:
  パーツ1 = Arduino Uno (Rev3)
  part = Resistor [tolerance=±5% resistance=220 package=THT]
  LED1 = LED - 5mm [color="Red (633nm)" package="5 mm [THT]"]

nets:
  N1: パーツ1.D13/SCK, part.Pin_1
  N2: パーツ1.GND, LED1.cathode
  N3: part.Pin_0, LED1.anode
