# Fritzing sketch sketch_pressure (saved by Fritzing 0.9.2b)
breadboards: 1

parts:
  パーツ1 = Arduino Uno (Rev3)
  R1 = Resistor [tolerance=±5% resistance=220 package=THT]
  LED1 = LED - 5mm [color="Red (633nm)" package="5 mm [THT]"]
  J2 = Basic Force Sensing Resistor (FSR) [package=THT]
  R2 = Resistor [tolerance=±5% resistance=10k package=THT]

nets:
  N1: パーツ1.A0, J2.pin_1, R2.Pin_0
  N2: パーツ1.GND, LED1.cathode, J2.pin_0
  N3: パーツ1.D6_PWM, R1.Pin_1
  N4: パーツ1.5V, R2.Pin_1
  N5: R1.Pin_0, LED1.anode
