# Fritzing sketch sketch_pwm (saved by Fritzing 0.9.2b)
breadboards: 1

parts:
  パーツ1 = Arduino Uno (Rev3)
  R1 = Resistor [tolerance=±5% resistance=220 package=THT]
  LED1 = LED - 5mm [color="Red (633nm)" package="5 mm [THT]"]

nets:
  N1: パーツ1.GND, LED1.cathode
  N2: パーツ1.D6_PWM, R1.Pin_1
  N3: R1.Pin_0, LED1.anode
