# Fritzing sketch sketch_switch (saved by Fritzing 0.9.2b)
breadboards: 1

parts:
  パーツ1 = Arduino Uno (Rev3)
  R1 = Resistor [tolerance=±5% resistance=10k package=THT]
  S1 = Pushbutton [package="[THT]"]
  J1 = Piezo Speaker

nets:
  N1: パーツ1.D12/MISO, J1.pin2
  N2: パーツ1.GND, S1.Pin_3, S1.Pin_4, J1.pin1
  N3: パーツ1.D5_PWM, R1.Pin_0, S1.Pin_1, S1.Pin_2
  N4: パーツ1.5V, R1.Pin_1
