# Fritzing sketch sketch_temp (saved by Fritzing 0.9.2b)
breadboards: 1

parts:
  パーツ1 = Arduino Uno (Rev3)
  T1 = TMP36 Temperature Sensor [package="TO92 [THT]"]

nets:
  N1: パーツ1.A0, T1.Vout
  N2: パーツ1.5V, T1.+Vs
  GND: パーツ1.GND, T1.GND
